// Logisim project Software.circ as structural Verilog: 1 circuit, main circuit main
module main (
  input  [7:0] xball,
  input  [7:0] yball,
  input  [7:0] vxy,
  input  clock,
  output [4:0] rightYin
);

  wire and_3_out, cdm_8_mark5_1_p2, cdm_8_mark5_1_p3, data, f3, f4, f5, instr, IO_3_2_out, IO_3_out,
       IO_4_out, IO_5_out, not_1_out, port, rd_d, rd_wr, wr_d;
  wire [2:0] register_1_q;
  wire [7:0] addr, cdm_8_mark5_1_p6, cdm_8_mark5_1_p7, controlled_buffer_2_out;

  Comparator comparator_1 (.a(addr), .b(8'hf3), .eq(f3));  // open: gt, lt
  Comparator comparator_2 (.a(addr), .b(8'hf4), .eq(f4));  // open: gt, lt
  Comparator comparator_3 (.a(addr), .b(8'hf5), .eq(f5));  // open: gt, lt
  Decoder #(.disabled(0)) decoder_1 (.out0(instr), .out1(data), .sel(cdm_8_mark5_1_p2), .en(cdm_8_mark5_1_p3));
  // CdM_8_mark5 cdm_8_mark5_1: pin names not known; wires that end beside it: clock, cdm_8_mark5_1_p2, cdm_8_mark5_1_p3, rd_wr, addr, cdm_8_mark5_1_p6, cdm_8_mark5_1_p7
  not not_1 (not_1_out, rd_wr);
  assign cdm_8_mark5_1_p7 = rd_wr ? controlled_buffer_2_out : 8'bz;  // Controlled_Buffer controlled_buffer_1
  and and_1 (rd_d, rd_wr, cdm_8_mark5_1_p2);
  and and_2 (wr_d, ~rd_wr, cdm_8_mark5_1_p2);  // AND_Gate
  assign controlled_buffer_2_out = not_1_out ? cdm_8_mark5_1_p6 : 8'bz;  // Controlled_Buffer controlled_buffer_2
  and and_3 (and_3_out, port, data);
  ROM rom_1 (.addr(addr), .data(controlled_buffer_2_out), .sel(instr));
  RAM ram_1 (.addr(addr), .data(controlled_buffer_2_out), .sel(and_3_out), .clk(clock), .ld(rd_wr));  // open: clr
  nor nor_1 (port, IO_4_out, IO_5_out, IO_3_out);
  assign controlled_buffer_2_out = IO_5_out ? yball : 8'bz;  // Controlled_Buffer controlled_buffer_3
  and IO_3 (IO_3_out, rd_d, f3);
  assign controlled_buffer_2_out = IO_3_out ? vxy : 8'bz;  // Controlled_Buffer controlled_buffer_4
  and IO_4 (IO_4_out, rd_d, f4);
  assign controlled_buffer_2_out = IO_4_out ? xball : 8'bz;  // Controlled_Buffer controlled_buffer_5
  and IO_5 (IO_5_out, rd_d, f5);
  and IO_3_2 (IO_3_2_out, wr_d, f3);
  Register register_1 (
    .D(controlled_buffer_2_out), .en(IO_3_2_out), .Q({rightYin, register_1_q}), .clk(clock));  // open: clr

  // Notes on the sheet:
  //   Note: 
  //   comparing addresses with values F3, F4 and F5 for writing and reading data
  //   instr memory 
  //   data memory 
  //   contents of rom_1 (hex, n*v repeats v):
  //   ff d1 f3 d2 f4 d3 f5 b5 ba bf c3 99 99 99 d0 4 44 e0 16 d0 f8 51 d3 e0 3e 9a d0 7f 42 d3 0 5 e5 49
  //   d0 fc 71 e1 2f 96 e2 2b 8f 96 e2 2f 8f d0 fd 71 e1 3d 8 96 e2 39 8f 12 e2 3d 8f d0 fe 71 e1 46 96 e2
  //   46 8f 86 ee 65 d0 3 71 e1 57 2 96 e3 53 8f 12 e3 57 8f d0 2 71 e1 60 96 e3 60 8f 5 e1 65 d2 0 c4 12
  //   9b e3 6b 86 d1 f3 a6 ee
  //   Note: 
  //   Note: 
  //   in the register and returned it to the controller 
  //   new coordinate of the right bat read at address F3 is stored 
  //   RAM needs to know if we are reading data from one of the ports
  //   Note: 
  //   Note: 
  //   Note: 
  //   the x coordinate of the ball
  //   is read at the address F4
  //   the y coordinate of the ball
  //   is read at the address F5
  //   ball's velocity is read at the address F3
endmodule
